# Fritzing sketch AcetoneBox (saved by Fritzing 0.9.3b)
perfboards: 1

parts:
  Часть1 = Arduino Nano (Rev3.0)
  S1 = Pushbutton [package="[THT]"]
  Q1 = Basic FET N-Channel [package="TO220 [THT]"]
  S2 = Toggle Switch [package=THT]
  J2 = Piezo Speaker
  R1 = Resistor [tolerance=±5% resistance=220 package=THT]
  D1 = Zener Diode [part_number=1N4732A breakdown_voltage=3.6V package="300 mil [THT]"]
  J1 = Screw terminal - 2 pins [package=THT]
  LED2 = 7-SEGMENT-4DIGIT [package=7-segment-4digit]  # not connected
  R2 = Resistor [tolerance=±5% resistance=220 package=THT]
  R3 = Resistor [tolerance=±5% resistance=220 package=THT]
  R4 = Resistor [tolerance=±5% resistance=220 package=THT]
  R5 = Resistor [tolerance=±5% resistance=220 package=THT]
  U1 = mystery part, 8 pins [chip_label="x2 tp4056"]
  U2 = BATTERY-2 [package=battery-aa]
  U3 = BATTERY-2 [package=battery-aa]

nets:
  N1: Часть1.GND, S1.Pin_1, S1.Pin_2, Q1.drain, S2.COM, J2.pin1
  N2: Часть1.D3, R1.Pin_1
  N3: Часть1.D9, R4.Pin_1
  N4: Часть1.D10, R3.Pin_1
  N5: Часть1.D11/MOSI, R5.Pin_1
  N6: Часть1.D12/MISO, R2.Pin_0
  N7: Часть1.VIN, D1.cathode, J1.pin1, U1.pin8
  N8: Часть1.A5, J2.pin2
  N9: Часть1.A4, S1.Pin_3, S1.Pin_4
  N10: Q1.gate, R1.Pin_0
  N11: Q1.source, D1.anode, J1.pin2
  N12: S2.L2, U1.pin1
  N13: U1.pin2, U2.-1
  N14: U1.pin3, U2.+1
  N15: U1.pin4, U1.pin5
  N16: U1.pin6, U3.-1
  N17: U1.pin7, U3.+1

notes:
  6x7dots 4digit 7segment
  4pin rounded buzzer
  18650 lipo
  tp4056 or another lipo saver
